// Logisim project imm-gen.circ as structural Verilog: 1 circuit, main circuit imm_gen
module imm_gen (
  input  [31:0] Instruction,
  input  [2:0] ImmSel,
  output [31:0] Immediate
);

  wire [11:0] Utype;
  wire [31:0] Btype, Immediate1, Immediate2, Itype, Jtype, Stype;
  wire [31:1] Immediate5;
  wire [31:12] Immediate3, Immediate4;

  Multiplexer #(.select(3), .width(32)) multiplexer_1 (
    .in0(Immediate1), .in1(Immediate2), .in2({Immediate3, Btype[7], Btype[30:25], Btype[11:8], 1'b0}),
    .in3({Immediate4, {12{1'b0}}}), .in4({Immediate5, 1'b0}), .out(Immediate), .sel(ImmSel));  // open: in5, in6, in7
  Demultiplexer #(.select(3), .width(32)) demultiplexer_1 (
    .out0({Itype[31], Immediate1[10:0], Itype[19:0]}),
    .out1({Stype[31], Immediate2[10:5], Stype[24:12], Immediate2[4:0], Stype[6:0]}), .out2(Btype),
    .out3({Immediate4, Utype}),
    .out4({Jtype[31], Immediate5[10:1], Immediate5[11], Immediate5[19:12], Jtype[11:0]}), .in(Instruction),
    .sel(ImmSel));  // open: out5, out6, out7
  assign Immediate5[31:20] = {{11{Jtype[31]}}, Jtype[31]};  // Bit_Extender bit_extender_1
  assign Immediate1[31:11] = {{20{Itype[31]}}, Itype[31]};  // Bit_Extender bit_extender_2
  assign Immediate2[31:11] = {{20{Stype[31]}}, Stype[31]};  // Bit_Extender bit_extender_3
  assign Immediate3 = {{19{Btype[31]}}, Btype[31]};  // Bit_Extender bit_extender_4

  // Other names for the same wires on the sheet: Itype[30:20] = Immediate1[10:0];
  //   Stype (some bits) = Immediate2[10:0]; Immediate3[11:1] = {Btype[7], Btype[30:25], Btype[11:8]};
  //   Utype[31:12] = Immediate4; Jtype[30:12] = {Immediate5[10:1], Immediate5[11], Immediate5[19:12]}

  // Notes on the sheet:
  //   INPUTS to your circuit
  //   DON'T CHANGE THE LOCATIONS OF THE INPUTS AND OUTPUTS!
  //   OUTPUT from your circuit
endmodule
