// Logisim project partial-load.circ as structural Verilog: 1 circuit, main circuit partial_load
module partial_load (
  input  [31:0] Instruction,
  input  [31:0] MemAddress,
  input  [31:0] DataFromMem,
  output [31:0] DataToReg
);

  wire [31:0] bit_extender_1_out, bit_extender_2_out, bit_extender_3_out, bit_extender_4_out,
       bit_extender_5_out, bit_extender_6_out, bit_extender_7_out, DataToReg1, DataToReg2, DataToReg3,
       demultiplexer_2_out0, demultiplexer_2_out1, demultiplexer_2_out2, demultiplexer_2_out3,
       demultiplexer_3_out0, demultiplexer_3_out1, demultiplexer_3_out2, lb, lh, lw;

  Demultiplexer #(.select(2), .width(32)) demultiplexer_1 (
    .out0(lb), .out1(lh), .out2(lw), .in(MemAddress), .sel(Instruction[13:12]));  // open: out3
  Multiplexer #(.select(2), .width(32)) multiplexer_1 (
    .in0(DataToReg1), .in1(DataToReg2), .in2(DataToReg3), .out(DataToReg), .sel(Instruction[13:12]));  // open: in3
  Demultiplexer #(.select(2), .width(32)) demultiplexer_2 (
    .out0(demultiplexer_2_out0), .out1(demultiplexer_2_out1), .out2(demultiplexer_2_out2),
    .out3(demultiplexer_2_out3), .in(DataFromMem), .sel(lb[1:0]));
  Demultiplexer #(.select(2), .width(32)) demultiplexer_3 (
    .out0(demultiplexer_3_out0), .out1(demultiplexer_3_out1), .out2(demultiplexer_3_out2), .in(DataFromMem),
    .sel(lh[1:0]));  // open: out3
  Demultiplexer #(.select(2), .width(32)) demultiplexer_4 (
    .out0(DataToReg3), .in(DataFromMem), .sel(lw[1:0]));  // open: out1, out2, out3
  assign bit_extender_1_out = {{24{demultiplexer_2_out0[7]}}, demultiplexer_2_out0[7:0]};  // Bit_Extender bit_extender_1
  assign bit_extender_2_out = {{24{demultiplexer_2_out1[15]}}, demultiplexer_2_out1[15:8]};  // Bit_Extender bit_extender_2
  assign bit_extender_3_out = {{24{demultiplexer_2_out2[23]}}, demultiplexer_2_out2[23:16]};  // Bit_Extender bit_extender_3
  assign bit_extender_4_out = {{24{demultiplexer_2_out3[31]}}, demultiplexer_2_out3[31:24]};  // Bit_Extender bit_extender_4
  assign bit_extender_5_out = {{16{demultiplexer_3_out0[15]}}, demultiplexer_3_out0[15:0]};  // Bit_Extender bit_extender_5
  assign bit_extender_6_out = {{16{demultiplexer_3_out1[23]}}, demultiplexer_3_out1[23:8]};  // Bit_Extender bit_extender_6
  assign bit_extender_7_out = {{16{demultiplexer_3_out2[31]}}, demultiplexer_3_out2[31:16]};  // Bit_Extender bit_extender_7
  Multiplexer #(.select(2), .width(32)) multiplexer_2 (
    .in0(bit_extender_1_out), .in1(bit_extender_2_out), .in2(bit_extender_3_out), .in3(bit_extender_4_out),
    .out(DataToReg1), .sel(lb[1:0]));
  Multiplexer #(.select(2), .width(32)) multiplexer_3 (
    .in0(bit_extender_5_out), .in1(bit_extender_6_out), .in2(bit_extender_7_out), .out(DataToReg2),
    .sel(lh[1:0]));  // open: in3

  // Notes on the sheet:
  //   INPUTS to your circuit
  //   DON'T CHANGE THE LOCATIONS OF THE INPUTS AND OUTPUTS!
  //   OUTPUT from your circuit
endmodule
