// Logisim project partial-store.circ as structural Verilog: 1 circuit, main circuit partial_store
module partial_store (
  input  [31:0] Instruction,
  input  [31:0] MemAddress,
  input  [31:0] DataFromReg,
  input  MemWEn,
  output [3:0] MemWriteMask,
  output [31:0] DataToMem
);

  wire [3:0] MemWriteMask1, MemWriteMask2, MemWriteMask3, MemWriteMask4;
  wire [31:0] DataToMem1, DataToMem2, DataToMem3, demultiplexer_2_out0, demultiplexer_2_out1,
       demultiplexer_2_out2, demultiplexer_2_out3, demultiplexer_3_out0, demultiplexer_3_out2,
       demultiplexer_4_out0, sb, sh, sw;

  Demultiplexer #(.select(2), .width(32)) demultiplexer_1 (
    .out0(sb), .out1(sh), .out2(sw), .in(MemAddress), .sel(Instruction[13:12]));  // open: out3
  Multiplexer #(.select(2), .width(32)) multiplexer_1 (
    .in0(DataToMem1), .in1(DataToMem2), .in2(DataToMem3), .out(DataToMem), .sel(Instruction[13:12]));  // open: in3
  Multiplexer #(.select(2), .width(4)) multiplexer_2 (
    .in0(4'b0001), .in1(4'b0010), .in2(4'b0100), .in3(4'b1000), .out(MemWriteMask1), .sel(sb[1:0]));
  Multiplexer #(.select(2), .width(4)) multiplexer_3 (
    .in0(4'b0011), .in2(4'b1100), .out(MemWriteMask2), .sel(sh[1:0]));  // open: in1, in3
  Multiplexer #(.select(2), .width(4)) multiplexer_4 (
    .in0(4'b1111), .out(MemWriteMask3), .sel(sw[1:0]));  // open: in1, in2, in3
  Demultiplexer #(.select(2), .width(32)) demultiplexer_2 (
    .out0(demultiplexer_2_out0), .out1(demultiplexer_2_out1), .out2(demultiplexer_2_out2),
    .out3(demultiplexer_2_out3), .in(DataFromReg), .sel(sb[1:0]));
  Demultiplexer #(.select(2), .width(32)) demultiplexer_3 (
    .out0(demultiplexer_3_out0), .out2(demultiplexer_3_out2), .in(DataFromReg), .sel(sh[1:0]));  // open: out1, out3
  Multiplexer #(.select(2), .width(4)) multiplexer_5 (
    .in0(MemWriteMask1), .in1(MemWriteMask2), .in2(MemWriteMask3), .out(MemWriteMask4),
    .sel(Instruction[13:12]));  // open: in3
  Demultiplexer #(.select(2), .width(32)) demultiplexer_4 (
    .out0(demultiplexer_4_out0), .in(DataFromReg), .sel(sw[1:0]));  // open: out1, out2, out3
  Multiplexer #(.width(4)) multiplexer_6 (.in0(4'b0000), .in1(MemWriteMask4), .out(MemWriteMask), .sel(MemWEn));
  Multiplexer #(.select(2), .width(32)) multiplexer_7 (
    .in0({{24{1'b0}}, demultiplexer_2_out0[7:0]}), .in1({{16{1'b0}}, demultiplexer_2_out1[7:0], {8{1'b0}}}),
    .in2({{8{1'b0}}, demultiplexer_2_out2[7:0], {16{1'b0}}}), .in3({demultiplexer_2_out3[7:0], {24{1'b0}}}),
    .out(DataToMem1), .sel(sb[1:0]));
  Multiplexer #(.select(2), .width(32)) multiplexer_8 (
    .in0({{16{1'b0}}, demultiplexer_3_out0[15:0]}), .in2({demultiplexer_3_out2[15:0], {16{1'b0}}}),
    .out(DataToMem2), .sel(sh[1:0]));  // open: in1, in3
  Multiplexer #(.select(2), .width(32)) multiplexer_9 (
    .in0(demultiplexer_4_out0), .out(DataToMem3), .sel(sw[1:0]));  // open: in1, in2, in3

  // Notes on the sheet:
  //   INPUTS to your circuit
  //   DON'T CHANGE THE LOCATIONS OF THE INPUTS AND OUTPUTS!
  //   OUTPUT from your circuit
endmodule
