// Logisim project cpu-harness.circ as structural Verilog: 1 circuit, main circuit cpu_harness
module cpu_harness (
  input  [31:0] Instruction,
  input  clk,
  output [31:0] ProgramCounter,
  output [31:0] ra,
  output [31:0] sp,
  output [31:0] t0,
  output [31:0] t1,
  output [31:0] t2,
  output [31:0] s0,
  output [31:0] s1,
  output [31:0] a0
);

  wire [3:0] cpu_1_memwritemask;
  wire [31:0] cpu_1_memaddress, cpu_1_memwritedata, mem_1_memreaddata;

  cpu cpu_1 (
    .clk(clk), .Instruction(Instruction), .MemReadData(mem_1_memreaddata), .MemAddress(cpu_1_memaddress),
    .ProgramCounter(ProgramCounter), .ra(ra), .sp(sp), .t0(t0), .t1(t1), .t2(t2), .s0(s0), .s1(s1), .a0(a0),
    .MemWriteMask(cpu_1_memwritemask), .MemWriteData(cpu_1_memwritedata));
  mem mem_1 (
    .MemAddress(cpu_1_memaddress), .MemWriteMask(cpu_1_memwritemask), .MemWriteData(cpu_1_memwritedata),
    .clk(clk), .MemReadData(mem_1_memreaddata));

  // Notes on the sheet:
  //   YOUR CPU SHOULD FIT IN HERE!
  //   Right click the CPU circuit and click "View cpu" to view the CPU
  //   <- Don't worry if this wire is red
endmodule
