// Logisim project partial-load-harness.circ as structural Verilog: 1 circuit, main circuit main
module main (
  output [7:0] Test,
  output [31:0] DataToReg,
  output halt,
  output [31:0] Instruction,
  output [31:0] MemAddress,
  output [31:0] DataFromMem
);

  wire clock_1_out;
  wire [7:0] adder_1_out;

  Clock clock_1 (.out(clock_1_out));
  Adder adder_1 (.a(8'h1), .b(Test), .out(adder_1_out));  // open: cin, cout
  Register register_1 (.D(adder_1_out), .clk(clock_1_out), .Q(Test));  // open: en, clr
  ROM #(.dataWidth(32)) rom_1 (.addr(Test), .data(Instruction));
  Comparator comparator_1 (.a(Test), .b({8{1'b0}}), .eq(halt));  // open: gt, lt
  // Probe on MemAddress
  // Probe on Instruction
  // Probe on DataFromMem
  ROM #(.dataWidth(32)) rom_2 (.addr(Test), .data(MemAddress));
  partial_load partial_load_1 (
    .Instruction(Instruction), .MemAddress(MemAddress), .DataFromMem(DataFromMem), .DataToReg(DataToReg));
  ROM #(.dataWidth(32)) rom_3 (.addr(Test), .data(DataFromMem));

  // Notes on the sheet:
  //   partial_load must fit here!
  //   There should be no red or blue wires, and the result should not be all X's
endmodule
