// Logisim project jump-far.circ as structural Verilog: 1 circuit, main circuit run_main
module run_main (
  output [31:0] ra,
  output [31:0] sp,
  output [31:0] t0,
  output [31:0] t1,
  output [31:0] t2,
  output [31:0] s0,
  output [31:0] s1,
  output [31:0] a0,
  output [31:0] RequestedAddress,
  output [31:0] RequestedInstruction,
  output [15:0] TimeStep,
  output halt
);

  wire clk;

  Clock clock_1 (.out(clk));
  // Probe on RequestedAddress
  cpu_harness cpu_harness_1 (
    .Instruction(RequestedInstruction), .clk(clk), .ProgramCounter(RequestedAddress), .ra(ra), .sp(sp),
    .t0(t0), .t1(t1), .t2(t2), .s0(s0), .s1(s1), .a0(a0));
  ROM #(.addrWidth(14), .dataWidth(32)) rom_1 (.addr(RequestedAddress[15:2]), .data(RequestedInstruction));
  // Probe on RequestedInstruction
  Counter #(.max('hffff), .width(16)) counter_1 (.clk(clk), .Q(TimeStep));  // open: clr, load, up, count, D, carry
  Comparator #(.width(16)) comparator_1 (.a(TimeStep), .b(16'h7), .eq(halt));  // open: gt, lt

  // Other names for the same wires on the sheet: Instruction[31:0] = RequestedInstruction;
  //   ProgramCounter[31:0] = RequestedAddress

  // Notes on the sheet:
  //   contents of rom_1 (hex, n*v repeats v):
  //   40b7 ff808093 8067 100413 200413 300413 400413 500413 600413 700413 800413 900413 a00413 b00413
  //   c00413 d00413 e00413 f00413 1000413 1100413 1200413 1300413 1400413 1500413 1600413 1700413 1800413
  //   1900413 1a00413 1b00413 1c00413 1d00413 1e00413 1f00413 2000413 2100413 2200413 2300413 2400413
  //   2500413 2600413 2700413 2800413 2900413 2a00413 2b00413 2c00413 2d00413 2e00413 2f00413 3000413
  //   3100413 3200413 3300413 3400413 3500413 3600413 3700413 3800413 3900413 3a00413 3b00413 3c00413
  //   3d00413 3e00413 3f00413 4000413 4100413 4200413 4300413 4400413 4500413 4600413 4700413 4800413
  //   4900413 4a00413 4b00413 4c00413 4d00413 4e00413 4f00413 5000413 5100413 5200413 5300413 5400413
  //   5500413 5600413 5700413 5800413 5900413 5a00413 5b00413 5c00413 5d00413 5e00413 5f00413 6000413
  //   6100413 6200413 6300413 6400413 6500413 6600413 6700413 6800413 6900413 6a00413 6b00413 6c00413
  //   6d00413 6e00413 6f00413 7000413 7100413 7200413 7300413 7400413 7500413 7600413 7700413 7800413
  //   7900413 7a00413 7b00413 7c00413 7d00413 7e00413 7f00413 8000413 8100413 8200413 8300413 8400413
  //   8500413 8600413 8700413 8800413 8900413 8a00413 8b00413 8c00413 8d00413 8e00413 8f00413 9000413
  //   9100413 9200413 9300413 9400413 9500413 9600413 9700413 9800413 9900413 9a00413 9b00413 9c00413
  //   9d00413 9e00413 9f00413 a000413 a100413 a200413 a300413 a400413 a500413 a600413 a700413 a800413
  //   a900413 aa00413 ab00413 ac00413 ad00413 ae00413 af00413 b000413 b100413 b200413 b300413 b400413
  //   b500413 b600413 b700413 b800413 b900413 ba00413 bb00413 bc00413 bd00413 be00413 bf00413 c000413
  //   c100413 c200413 c300413 c400413 c500413 c600413 c700413 c800413 c900413 ca00413 cb00413 cc00413
  //   cd00413 ce00413 cf00413 d000413 d100413 d200413 d300413 d400413 d500413 d600413 d700413 d800413
  //   d900413 da00413 db00413 dc00413 dd00413 de00413 df00413 e000413 e100413 e200413 e300413 e400413
  //   e500413 e600413 e700413 e800413 e900413 ea00413 eb00413 ec00413 ed00413 ee00413 ef00413 f000413
  //   f100413 f200413 f300413 f400413 f500413 f600413 f700413 f800413 f900413 fa00413 fb00413 fc00413
  //   fd00413 fe00413 ff00413 10000413 10100413 10200413 10300413 10400413 10500413 10600413 10700413
  //   10800413 10900413 10a00413 10b00413 10c00413 10d00413 10e00413 10f00413 11000413 11100413 11200413
  //   11300413 11400413 11500413 11600413 11700413 11800413 11900413 11a00413 11b00413 11c00413 11d00413
  //   11e00413 11f00413 12000413 12100413 12200413 12300413 12400413 12500413 12600413 12700413 12800413
  //   12900413 12a00413 12b00413 12c00413 12d00413 12e00413 12f00413 13000413 13100413 13200413 13300413
  //   13400413 13500413 13600413 13700413 13800413 13900413 13a00413 13b00413 13c00413 13d00413 13e00413
  //   13f00413 14000413 14100413 14200413 14300413 14400413 14500413 14600413 14700413 14800413 14900413
  //   14a00413 14b00413 14c00413 14d00413 14e00413 14f00413 15000413 15100413 15200413 15300413 15400413
  //   15500413 15600413 15700413 15800413 15900413 15a00413 15b00413 15c00413 15d00413 15e00413 15f00413
  //   16000413 16100413 16200413 16300413 16400413 16500413 16600413 16700413 16800413 16900413 16a00413
  //   16b00413 16c00413 16d00413 16e00413 16f00413 17000413 17100413 17200413 17300413 17400413 17500413
  //   17600413 17700413 17800413 17900413 17a00413 17b00413 17c00413 17d00413 17e00413 17f00413 18000413
  //   18100413 18200413 18300413 18400413 18500413 18600413 18700413 18800413 18900413 18a00413 18b00413
  //   18c00413 18d00413 18e00413 18f00413 19000413 19100413 19200413 19300413 19400413 19500413 19600413
  //   19700413 19800413 19900413 19a00413 19b00413 19c00413 19d00413 19e00413 19f00413 1a000413 1a100413
  //   1a200413 1a300413 1a400413 1a500413 1a600413 1a700413 1a800413 1a900413 1aa00413 1ab00413 1ac00413
  //   1ad00413 1ae00413 1af00413 1b000413 1b100413 1b200413 1b300413 1b400413 1b500413 1b600413 1b700413
  //   1b800413 1b900413 1ba00413 1bb00413 1bc00413 1bd00413 1be00413 1bf00413 1c000413 1c100413 1c200413
  //   1c300413 1c400413 1c500413 1c600413 1c700413 1c800413 1c900413 1ca00413 1cb00413 1cc00413 1cd00413
  //   1ce00413 1cf00413 1d000413 1d100413 1d200413 1d300413 1d400413 1d500413 1d600413 1d700413 1d800413
  //   1d9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
  //   Instruction Memory
  //   Halts Execution After Constant # of Clock Cycles
  //   Constant
endmodule
